// Logisim project full_adder.circ as structural Verilog: 1 circuit, main circuit main
module main (
  input  Carry_In,
  input  a,
  input  b,
  output s1,
  output Carry_Out
);

  wire and_1_out, and_2_out, xor_1_out;

  xor xor_1 (xor_1_out, a, b);
  and and_1 (and_1_out, a, b);
  or or_1 (Carry_Out, and_1_out, and_2_out);
  and and_2 (and_2_out, xor_1_out, Carry_In);
  xor xor_2 (s1, Carry_In, xor_1_out);
endmodule
