// Logisim project mux_2b.circ as structural Verilog: 1 circuit, main circuit main
module main (
  input  B_invert,
  input  a,
  input  b,
  output s
);

  wire and_1_out, and_2_out, not_1_out;

  not not_1 (not_1_out, B_invert);
  and and_1 (and_1_out, a, not_1_out);
  and and_2 (and_2_out, b, B_invert);
  or or_1 (s, and_1_out, and_2_out);
endmodule
