// Logisim project mux_4b.circ as structural Verilog: 1 circuit, main circuit main
module main (
  input  _01,
  input  _02,
  input  _03,
  input  _04,
  input  OP1,
  input  OP2,
  output out_7
);

  wire and_1_out, and_2_out, and_3_out, and_4_out, not_1_out, not_2_out;

  not not_1 (not_1_out, OP1);
  and and_1 (and_1_out, _01, not_2_out, not_1_out);
  and and_2 (and_2_out, _02, OP2, not_1_out);
  and and_3 (and_3_out, _03, not_2_out, OP1);
  and and_4 (and_4_out, _04, OP1, OP2);
  not not_2 (not_2_out, OP2);
  or or_1 (out_7, and_1_out, and_2_out, and_3_out, and_4_out);
endmodule
