// Logisim project ula_1b.circ as structural Verilog: 1 circuit, main circuit main
module main (
  input  B_Invert,
  input  Carry_In,
  input  a,
  input  b,
  input  OP0,
  input  OP1,
  output out_7,
  output Carry_Out
);

  wire and_1_out, main_1_s, main_2_s1, not_1_out, not_2_out, or_1_out;

  not not_1 (not_1_out, b);
  mux_2b_main main_1 (.a(b), .b(not_1_out), .B_invert(B_Invert), .s(main_1_s));
  and and_1 (and_1_out, a, main_1_s);
  or or_1 (or_1_out, a, main_1_s);
  not not_2 (not_2_out, a);
  full_adder_main main_2 (.a(a), .b(main_1_s), .Carry_In(Carry_In), .Carry_Out(Carry_Out), .s1(main_2_s1));
  mux_4b_main main_3 (
    ._01(and_1_out), ._02(or_1_out), ._03(not_2_out), ._04(main_2_s1), .OP1(OP0), .OP2(OP1), .out_7(out_7));
endmodule
