// Logisim project adder_4_bits.circ as structural Verilog: 1 circuit, main circuit main
module main (
  input  [3:0] A,
  input  [3:0] B,
  input  Carry_In,
  output [3:0] out_4,
  output Carry_out
);

  wire main_1_carry_out, main_2_carry_out, main_3_carry_out;

  full_adder_main main_1 (.A(B[0]), .B(A[0]), .Carry_In(Carry_In), .Carry_Out(main_1_carry_out), .Saida(out_4[0]));
  full_adder_main main_2 (
    .A(B[1]), .B(A[1]), .Carry_In(main_1_carry_out), .Carry_Out(main_2_carry_out), .Saida(out_4[1]));
  full_adder_main main_3 (
    .A(B[2]), .B(A[2]), .Carry_In(main_2_carry_out), .Carry_Out(main_3_carry_out), .Saida(out_4[2]));
  full_adder_main main_4 (.A(B[3]), .B(A[3]), .Carry_In(main_3_carry_out), .Carry_Out(Carry_out), .Saida(out_4[3]));
endmodule
