// Logisim project calculadora.circ as structural Verilog: 1 circuit, main circuit main
module main (
  input  [3:0] A,
  input  in_2,
  input  [3:0] B,
  output Overflow
);

  wire main_2_a_2, main_2_b_2, main_2_c_2, main_2_d_2, main_2_e, main_2_f, main_2_g, main_3_a_2, main_3_b_2,
       main_3_c_2, main_3_d_2, main_3_e, main_3_f, main_3_g, main_4_a_2, main_4_b_2, main_4_c_2, main_4_d_2,
       main_4_e, main_4_f, main_4_g;
  wire [3:0] main_1_out_4;

  adder_4_bits_main main_1 (.A(A), .B(B), .Carry_In(in_2), .out_4(main_1_out_4), .Carry_out(Overflow));
  decoder_main main_2 (
    .a(A[3]), .b(A[2]), .c(A[1]), .d(A[0]), .a_2(main_2_a_2), .b_2(main_2_b_2), .c_2(main_2_c_2),
    .d_2(main_2_d_2), .e(main_2_e), .f(main_2_f), .g(main_2_g));
  decoder_main main_3 (
    .a(main_1_out_4[3]), .b(main_1_out_4[2]), .c(main_1_out_4[1]), .d(main_1_out_4[0]), .a_2(main_3_a_2),
    .b_2(main_3_b_2), .c_2(main_3_c_2), .d_2(main_3_d_2), .e(main_3_e), .f(main_3_f), .g(main_3_g));
  decoder_main main_4 (
    .a(B[3]), .b(B[2]), .c(B[1]), .d(B[0]), .a_2(main_4_a_2), .b_2(main_4_b_2), .c_2(main_4_c_2),
    .d_2(main_4_d_2), .e(main_4_e), .f(main_4_f), .g(main_4_g));
  _7_Segment_Display u_7_segment_display_1 (
    .g(main_2_g), .f(main_2_f), .a(main_2_a_2), .b(main_2_b_2), .e(main_2_e), .d(main_2_d_2), .c(main_2_c_2));  // open: dp
  _7_Segment_Display u_7_segment_display_2 (
    .g(main_4_g), .f(main_4_f), .a(main_4_a_2), .b(main_4_b_2), .e(main_4_e), .d(main_4_d_2), .c(main_4_c_2));  // open: dp
  _7_Segment_Display u_7_segment_display_3 (
    .g(main_3_g), .f(main_3_f), .a(main_3_a_2), .b(main_3_b_2), .e(main_3_e), .d(main_3_d_2), .c(main_3_c_2));  // open: dp
endmodule
