// Logisim project full_adder.circ as structural Verilog: 1 circuit, main circuit main
module main (
  input  Carry_In,
  input  A,
  input  B,
  output Saida,
  output Carry_Out
);

  wire main_1_carry_out, main_1_saida, main_2_carry_out;

  half_adder_main main_1 (.A(A), .B(B), .Carry_Out(main_1_carry_out), .Saida(main_1_saida));
  or or_1 (Carry_Out, main_1_carry_out, main_2_carry_out);
  half_adder_main main_2 (.A(Carry_In), .B(main_1_saida), .Carry_Out(main_2_carry_out), .Saida(Saida));

  // Notes on the sheet:
  //   Somador Completo - 1 bit
  //   Rafael Amauri Diniz Augusto - 651047
endmodule
