// Logisim project half_adder.circ as structural Verilog: 1 circuit, main circuit main
module main (
  input  A,
  input  B,
  output Saida,
  output Carry_Out
);

  and and_1 (Carry_Out, B, A);
  xor xor_1 (Saida, A, B);

  // Notes on the sheet:
  //   Meio Somador
  //   Rafael Amauri Diniz Augusto - 651047
endmodule
