// Logisim project ula_4b.circ as structural Verilog: 1 circuit, main circuit main
module main (
  input  B_Invert,
  input  a3,
  input  a2,
  input  a1,
  input  a1_2,
  input  b3,
  input  b2,
  input  b0,
  input  b0_2,
  input  OP_0,
  input  OP_1,
  output s3,
  output s2,
  output s1,
  output s0,
  output out_16
);

  wire main_1_carry_out, main_2_carry_out, main_3_carry_out, main_4_carry_out;

  ula_1b_main main_1 (
    .a(a1_2), .b(b0_2), .B_Invert(B_Invert), .Carry_In(B_Invert), .OP0(OP_0), .OP1(OP_1),
    .Carry_Out(main_1_carry_out), .out_7(s0));
  ula_1b_main main_2 (
    .a(a1), .b(b0), .B_Invert(B_Invert), .Carry_In(main_1_carry_out), .OP0(OP_0), .OP1(OP_1),
    .Carry_Out(main_2_carry_out), .out_7(s1));
  ula_1b_main main_3 (
    .a(a2), .b(b2), .B_Invert(B_Invert), .Carry_In(main_2_carry_out), .OP0(OP_0), .OP1(OP_1),
    .Carry_Out(main_3_carry_out), .out_7(s2));
  ula_1b_main main_4 (
    .a(a3), .b(b3), .B_Invert(B_Invert), .Carry_In(main_3_carry_out), .OP0(OP_0), .OP1(OP_1),
    .Carry_Out(main_4_carry_out), .out_7(s3));
  xor xor_1 (out_16, main_4_carry_out, B_Invert);
endmodule
